# Fritzing sketch schematic (saved by Fritzing 0.9.3b)
stripboards: 1

parts:
  Q2 = NPN-Transistor [package="TO92 [THT]"]
  VCC1 = Battery block 9V
  U1 = ESP32S-HiLetgo [part_number=ESP32S-HiLetgo]
  U2 = Voltage Regulator - 5V [package="TO220 [THT]"]
  U2_2 = Voltage Regulator - 3.3V [package="TO220 [THT]"]
  J6 = Screw terminal - 2 pins [package=THT]
  J7 = Screw terminal - 2 pins [package=THT]
  J8 = Screw terminal - 2 pins [package=THT]
  M1 = DC Motor
  M2 = DC Motor
  hc-sr1 = hc-sr04
  J9 = Screw terminal - 2 pins [package=THT]
  J10 = Screw terminal - 2 pins [package=THT]

nets:
  N1: Q2.E, J7.pin1, J8.pin1, M1.pin_2, M2.pin_2
  N2: Q2.B, U1.GPIO2
  N3: Q2.C, VCC1.+, U2.input_voltage, U2_2.input_voltage, J6.pin1
  GND: VCC1.-, U1.GND, U2.GND, J6.pin2, J7.pin2, J8.pin2, M1.pin_1, M2.pin_1, hc-sr1.GND, J9.pin1
  N4: U1.GPIO27, hc-sr1.Trig, J10.pin1
  N5: U1.GPIO14, hc-sr1.Echo, J9.pin2
  N6: U1.VIN, U2_2.output_voltage
  N7: U1.GPIO22, U1.GPIO23
  N8: U2.output_voltage, hc-sr1.VCC, J10.pin2

custom parts:
  ESP32S-HiLetgo: HiLetgo ESP-WROOM-32 ESP32 ESP-32S Development Board 2.4GHz Dual-Mode WiFi + Bluetooth Dual Cores Microcontroller The ESP32 integrated with Antenna switches, RF Balun, power amplifiers, low-noise amplifiers, filters, and management modules, and the entire solution occupies the least area of PCB. 2.4 GHz Wi-Fi plus Bluetooth dual-mode chip, with TSMC Ultra-low power consumption 40nm technology,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
