# Fritzing sketch wsys (saved by Fritzing 0.9.3b)
breadboards: 1

parts:
  Q1 = NPN-Transistor [package="TO92 [THT]"]  # not connected
  Q2 = NPN-Transistor [package="TO92 [THT]"]  # not connected
  M1 = DC Motor
  M2 = DC Motor
  Part1 = Arduino Uno (Rev3)
  Part2 = Bluetooth HC-05 Macho

nets:
  GND: M1.pin_2, M2.pin_2, Part1.GND, Part2.GND
  N1: Part1.D0/RX, Part2.TXD
  N2: Part1.D1/TX, Part2.RXD
  5V: Part1.5V, Part2.VCC
